# Fritzing sketch DRONE_LAUNCH (saved by Fritzing 1.0.1rc)
breadboards: 1

parts:
  Heltec_ESP_32_V2 = Heltec WiFi LoRa 32 V2 [part_number=HTIT-WB32LA]
  WeMos_D1_Mini_Relay_Shield_V1 = WeMos D1 Mini Relay Shield V2  # not connected

nets:
  N1: Heltec_ESP_32_V2.pin_16, Heltec_ESP_32_V2.pin_17
  N2: Heltec_ESP_32_V2.pin_21, Heltec_ESP_32_V2.pin_22

notes:
  DRONE_LAUNCH
  GPIO 16 <
  ANTENNA >
