# Fritzing sketch PIR CALLBACK BUZZER (saved by Fritzing 1.0.1rc)
breadboards: 1

parts:
  Heltec_ESP_32_V2 = Heltec WiFi LoRa 32 V2 [part_number=HTIT-WB32LA]
  Mod2 = Passive Buzzer
  LED1 = LED - 3mm [color="Red (633nm)" current=0.030 package="3 mm [THT]"]
  LED2 = LED - 3mm [color="Green (570nm)" current=0.030 package="3 mm [THT]"]
  R1 = Resistor [tolerance=±5% resistance=470 package="2010 [SMD]"]
  Mod3 = Passive Buzzer

nets:
  N1: Heltec_ESP_32_V2.pin_1, Mod2.S
  N2: Heltec_ESP_32_V2.pin_16, Heltec_ESP_32_V2.pin_17, Mod2.NC, LED1.cathode
  N3: Heltec_ESP_32_V2.GND, Mod2.-, LED1.anode, R1.Pin_1, Mod3.-
  N4: Heltec_ESP_32_V2.pin_20, Mod3.S
  N5: Heltec_ESP_32_V2.pin_21, Heltec_ESP_32_V2.pin_22
  N6: Heltec_ESP_32_V2.pin_33, LED2.cathode
  N7: Heltec_ESP_32_V2.pin_36, Mod3.NC
  N8: LED2.anode, R1.Pin_0

notes:
  PIR CALLBACK BUZZER
  > GPIO12
  GPIO 16 <
  > GPIO 2
  ANTENNA >
  PIR#1 & PIR#2
