# Fritzing sketch PIR NO BUZZER (saved by Fritzing 1.0.1rc)
breadboards: 1

parts:
  Heltec_ESP_32_V2 = Heltec WiFi LoRa 32 V2 [part_number=HTIT-WB32LA]
  Mod3 = Passive Buzzer

nets:
  N1: Heltec_ESP_32_V2.pin_16, Heltec_ESP_32_V2.pin_17
  N2: Heltec_ESP_32_V2.GND, Mod3.-
  N3: Heltec_ESP_32_V2.pin_20, Mod3.S
  N4: Heltec_ESP_32_V2.pin_21, Heltec_ESP_32_V2.pin_22
  N5: Heltec_ESP_32_V2.pin_36, Mod3.NC

notes:
  PIR NO BUZZER
  GPIO 16 <
  ANTENNA >
  PIR#3
